# Fritzing sketch cat_timer (saved by Fritzing 0.9.2b)
breadboards: 1

parts:
  Part1 = Arduino Nano (Rev3.0)
  VCC1 = Battery
  LED1 = LED - 5mm [color="Red (633nm)" package="5 mm [THT]"]  # not connected
  S2 = Round Pushbutton
  R3 = Resistor [tolerance=±5% resistance=10k package=THT]

nets:
  N1: Part1.D12/MISO, S2.leg1, R3.Pin_0
  N2: VCC1.-, R3.Pin_1
